# Fritzing sketch breadboard (saved by Fritzing 0.6.3b)
breadboards: 1

parts:
  Arduino1 = Arduino
  S1 = Pushbutton [package="[THT]"]
  R1 = Resistor [tolerance=±5% resistance=10k package=THT]
  LED1 = LED - 5mm [color="Red (633nm)" package="5 mm [THT]"]
  R2 = Resistor [tolerance=±5% resistance=220 package=THT]
  U1 = mystery part, 8 pins [chip_label=MPU6050 spacing=300mil]

nets:
  N1: Arduino1.D13, R2.Pin_1
  N2: Arduino1.D2, S1.Pin_3, S1.Pin_4, R1.Pin_0
  N3: Arduino1.3V3, U1.pin1
  N4: Arduino1.+5V, S1.Pin_1, S1.Pin_2
  N5: Arduino1.GND, R1.Pin_1, LED1.cathode, U1.pin2
  N6: Arduino1.A4, U1.pin4
  N7: Arduino1.A5, U1.pin3
  N8: LED1.anode, R2.Pin_0

notes:
  VCC,GND,SCL,SDA,XDA,XCL,ADD,INT
